# Fritzing sketch reaktionstester (saved by Fritzing 0.9.3b)
breadboards: 1

parts:
  Bauteil1 = Arduino Uno (Rev3)
  LED4 = smd LED [color="Red (633nm)" package="0603 [SMD]"]
  R4 = Resistor [tolerance=±5% resistance=220 package=THT]
  R2 = Resistor [tolerance=±5% resistance=220 package=THT]
  LED5 = smd LED [color="Red (633nm)" package="0603 [SMD]"]
  LED3 = smd LED [color="Red (633nm)" package="0603 [SMD]"]
  S1 = Pushbutton [package=THT]
  LED2 = smd LED [color="Red (633nm)" package="0603 [SMD]"]
  R6 = Resistor [tolerance=±5% resistance=220 package=THT]
  R5 = Resistor [tolerance=±5% resistance=220 package=THT]
  R1 = Resistor [tolerance=±5% resistance=220 package=THT]
  LED1 = smd LED [color="Red (633nm)" package="0603 [SMD]"]
  LED7 = smd LED [color="Red (633nm)" package="0603 [SMD]"]
  LED6 = smd LED [color="Red (633nm)" package="0603 [SMD]"]
  R8 = Resistor [tolerance=±5% resistance=10k package=THT]
  R3 = Resistor [tolerance=±5% resistance=220 package=THT]
  R9 = Resistor [tolerance=±5% resistance=220 package=THT]

nets:
  N1: Bauteil1.D8, LED5.anode
  N2: Bauteil1.D9_PWM, LED2.anode
  N3: Bauteil1.D10_PWM/SS, LED1.anode
  N4: Bauteil1.D11_PWM/MOSI, LED3.anode
  N5: Bauteil1.D12/MISO, LED4.anode
  N6: Bauteil1.D2, S1.leg1, R8.Pin_0
  N7: Bauteil1.D6_PWM, LED7.anode
  N8: Bauteil1.D7, LED6.anode
  N9: Bauteil1.5V, S1.leg0
  N10: Bauteil1.GND, R4.Pin_1, R2.Pin_1, R6.Pin_1, R5.Pin_1, R1.Pin_1, R8.Pin_1, R3.Pin_1, R9.Pin_1
  N11: LED4.cathode, R9.Pin_0
  N12: R4.Pin_0, LED2.cathode
  N13: R2.Pin_0, LED6.cathode
  N14: LED5.cathode, R3.Pin_0
  N15: LED3.cathode, R6.Pin_0
  N16: R5.Pin_0, LED1.cathode
  N17: R1.Pin_0, LED7.cathode
